# Fritzing sketch arduino_google_earth (saved by Fritzing 0.8.7b)
breadboards: 1

parts:
  パーツ1 = Arduino Uno (Rev3)  # not connected
  パーツ2 = Arduino XBee Shield
  U1 = XBEE-1 [package=xbee-1_lock]  # not connected
  GY1 = MPU-6050 Board GY-521 [form="♀ (female)" package=THT]
  S1 = Pushbutton [package="[THT]"]
  S2 = Pushbutton [package="[THT]"]
  S3 = Pushbutton [package="[THT]"]
  R1 = Resistor [package="2010 [SMD]"]
  R2 = Resistor [package="2010 [SMD]"]
  R3 = Resistor [package="2010 [SMD]"]

nets:
  N1: パーツ2.D10, パーツ2.5V, GY1.pin2, R1.Pin_0, R2.Pin_0, R3.Pin_0
  N2: パーツ2.A4, GY1.pin4
  N3: パーツ2.A5, GY1.pin3
  N4: パーツ2.D_RX, GY1.pin8
  N5: パーツ2.D8, S1.Pin_3, S1.Pin_4, R1.Pin_1
  N6: パーツ2.D9, S2.Pin_3, R2.Pin_1
  N7: パーツ2.GND, GY1.pin1, S1.Pin_1, S1.Pin_2, S3.Pin_1, S3.Pin_2
  N8: S3.Pin_3, S3.Pin_4, R3.Pin_1

custom parts:
  MPU-6050 Board GY-521: Acelerometro y Giroscopio MPU-6050 Board GY-521
